// Logisim project RegisterFile.circ as structural Verilog: 3 circuits, main circuit main
module main (
  input  select0,
  input  select1,
  input  write_enable,
  input  [2:0] data_in,
  output [2:0] data_out
);

  wire and_1_out, and_2_out, and_3_out, and_4_out, clock_1_out, n4dc_1_out0, n4dc_1_out1, n4dc_1_out2,
       n4dc_1_out3;
  wire [2:0] register_1_q, register_2_q, register_3_q, register_4_q;

  _4dc u_4dc_1 (
    .select0(select0), .select1(select1), .out0(n4dc_1_out0), .out1(n4dc_1_out1), .out2(n4dc_1_out2),
    .out3(n4dc_1_out3));
  and and_1 (and_1_out, n4dc_1_out0, write_enable);
  and and_2 (and_2_out, n4dc_1_out1, write_enable);
  and and_3 (and_3_out, n4dc_1_out2, write_enable);
  and and_4 (and_4_out, n4dc_1_out3, write_enable);
  Register #(.width(3)) register_1 (.D(data_in), .en(and_1_out), .Q(register_1_q), .clk(clock_1_out));  // open: clr
  Register #(.width(3)) register_2 (.D(data_in), .en(and_2_out), .Q(register_2_q), .clk(clock_1_out));  // open: clr
  Register #(.width(3)) register_3 (.D(data_in), .en(and_3_out), .Q(register_3_q), .clk(clock_1_out));  // open: clr
  Register #(.width(3)) register_4 (.D(data_in), .en(and_4_out), .Q(register_4_q), .clk(clock_1_out));  // open: clr
  Clock clock_1 (.out(clock_1_out));
  _4mp u_4mp_1 (
    .select_0(select0), .select_1(select1), .data0(register_1_q[0]), .data1(register_2_q[0]),
    .data2(register_3_q[0]), .data3(register_4_q[0]), .out_7(data_out[0]));
  _4mp u_4mp_2 (
    .select_0(select0), .select_1(select1), .data0(register_1_q[1]), .data1(register_2_q[1]),
    .data2(register_3_q[1]), .data3(register_4_q[1]), .out_7(data_out[1]));
  _4mp u_4mp_3 (
    .select_0(select0), .select_1(select1), .data0(register_1_q[2]), .data1(register_2_q[2]),
    .data2(register_3_q[2]), .data3(register_4_q[2]), .out_7(data_out[2]));
endmodule

module _4mp (
  input  select_0,
  input  select_1,
  input  data0,
  input  data1,
  input  data2,
  input  data3,
  output out_7
);

  wire and_1_out, and_2_out, and_3_out, and_4_out, not_1_out, not_2_out, not_3_out, not_4_out;

  not not_1 (not_1_out, select_0);
  not not_2 (not_2_out, select_1);
  not not_3 (not_3_out, select_1);
  not not_4 (not_4_out, select_0);
  and and_1 (and_1_out, not_1_out, not_2_out, data0);
  and and_2 (and_2_out, select_0, not_3_out, data1);
  and and_3 (and_3_out, not_4_out, select_1, data2);
  and and_4 (and_4_out, select_0, select_1, data3);
  or or_1 (out_7, and_1_out, and_2_out, and_3_out, and_4_out);
endmodule

module _4dc (
  input  select0,
  input  select1,
  output out0,
  output out1,
  output out2,
  output out3
);

  wire not_1_out, not_2_out, not_3_out, not_4_out;

  not not_1 (not_1_out, select0);
  not not_2 (not_2_out, select1);
  not not_3 (not_3_out, select1);
  not not_4 (not_4_out, select0);
  and and_1 (out0, not_1_out, not_2_out);
  and and_2 (out1, select0, not_3_out);
  and and_3 (out2, not_4_out, select1);
  and and_4 (out3, select0, select1);
endmodule
