// Logisim project ALU_Control.circ as structural Verilog: 1 circuit, main circuit ALU Control
module ALU_Control (
  input  [1:0] ALUOp,
  input  [5:0] Func,
  output [3:0] ALUCon
);

  wire and_1_out, not_1_out, not_2_out, not_3_out, or_1_out;

  and and_1 (and_1_out, ALUOp[1], Func[1]);
  and and_2 (ALUCon[0], ALUOp[1], or_1_out);
  or or_1 (or_1_out, Func[3], Func[0]);
  and and_3 (ALUCon[3], ALUOp[0], not_1_out);
  not not_1 (not_1_out, ALUOp[0]);
  or or_2 (ALUCon[2], ALUOp[0], and_1_out);
  not not_2 (not_2_out, ALUOp[1]);
  or or_3 (ALUCon[1], not_2_out, not_3_out);
  not not_3 (not_3_out, Func[2]);
endmodule
