// Logisim project CPU.circ as structural Verilog: 1 circuit, main circuit CPU
module CPU (
);

  wire alu_1_zero, and_1_out, clock_1_out, main_control_1_p2, main_control_1_p3, main_control_1_p4,
       main_control_1_p5, main_control_1_p6, main_control_1_p7, main_control_1_p8, main_control_1_p9;
  wire [3:0] undriven;
  wire [4:0] multiplexer_1_out;
  wire [31:0] adder_1_out, adder_2_out, alu_1_output, bit_extender_1_out, multiplexer_2_out,
       multiplexer_3_out, multiplexer_4_out, PC_q, ram_1_data, registerfile_1_read0_2,
       registerfile_1_read1_2, rom_1_data, shifter_1_out;

  Register #(.width(32)) PC (.D(multiplexer_3_out), .Q(PC_q), .clk(clock_1_out));  // open: en, clr
  Clock clock_1 (.out(clock_1_out));
  Adder #(.width(32)) adder_1 (.a(PC_q), .b(32'h4), .out(adder_1_out));  // open: cin, cout
  ROM #(.addrWidth(6), .dataWidth(32)) rom_1 (.addr(PC_q[7:2]), .data(rom_1_data));  // open: sel
  // Main_Control main_control_1: pin names not known; wires that end beside it: rom_1_data[31:26], main_control_1_p2, main_control_1_p3, main_control_1_p4, main_control_1_p5, main_control_1_p6, main_control_1_p7, main_control_1_p8, main_control_1_p9
  Multiplexer #(.width(5), .enable("false")) multiplexer_1 (
    .in0(rom_1_data[20:16]), .in1(rom_1_data[15:11]), .out(multiplexer_1_out), .sel(main_control_1_p2));
  RegisterFile registerfile_1 (
    .WriteRegister(multiplexer_1_out), .WriteData(multiplexer_4_out), .Clock(clock_1_out),
    .Read1(rom_1_data[20:16]), .Read0(rom_1_data[25:21]), .RegisterWrite(main_control_1_p9),
    .Read0_2(registerfile_1_read0_2), .Read1_2(registerfile_1_read1_2));
  assign bit_extender_1_out = {{16{rom_1_data[15]}}, rom_1_data[15:0]};  // Bit_Extender bit_extender_1
  Multiplexer #(.width(32), .enable("false")) multiplexer_2 (
    .in0(registerfile_1_read1_2), .in1(bit_extender_1_out), .out(multiplexer_2_out), .sel(main_control_1_p8));
  // ALU_Control alu_control_1: pin names not known; wires that end beside it: rom_1_data[5:0], main_control_1_p6
  Adder #(.width(32)) adder_2 (.a(adder_1_out), .b(shifter_1_out), .out(adder_2_out));  // open: cin, cout
  Shifter #(.width(32)) shifter_1 (.in(bit_extender_1_out), .\dist (5'b00010), .out(shifter_1_out));
  ALU alu_1 (
    .A(registerfile_1_read0_2), .B(multiplexer_2_out), .Ainvert(undriven[3]), .BNegate(undriven[2]),
    .Operation(undriven[1:0]), .Output(alu_1_output), .Zero(alu_1_zero));
  and and_1 (and_1_out, main_control_1_p5, alu_1_zero);
  Multiplexer #(.width(32), .enable("false")) multiplexer_3 (
    .in0(adder_1_out), .in1(adder_2_out), .out(multiplexer_3_out), .sel(and_1_out));
  RAM #(.addrWidth(6), .dataWidth(32), .bus("separate")) ram_1 (
    .addr(alu_1_output[7:2]), .din(registerfile_1_read1_2), .data(ram_1_data), .str(main_control_1_p7),
    .clk(clock_1_out), .ld(main_control_1_p3));  // open: sel, clr
  Multiplexer #(.width(32), .enable("false")) multiplexer_4 (
    .in0(alu_1_output), .in1(ram_1_data), .out(multiplexer_4_out), .sel(main_control_1_p4));

  // Notes on the sheet:
  //   contents of rom_1 (hex, n*v repeats v):
  //   22 8c010000 8c220000 8c230004 432024 432825 ac040004 ac050008 1000ffff
endmodule
