// Logisim project RegisterFile.circ as structural Verilog: 1 circuit, main circuit RegisterFile
module RegisterFile (
  input  [4:0] Read1,
  input  [4:0] Read0,
  input  [4:0] WriteRegister,
  input  [31:0] WriteData,
  input  Clock,
  input  RegisterWrite,
  output [31:0] Read0_2,
  output [31:0] Read1_2
);

  wire and_1_out, and_2_out, and_3_out, and_4_out, and_5_out, and_6_out, and_7_out, decoder_1_out0,
       decoder_1_out1, decoder_1_out2, decoder_1_out3, decoder_1_out4, decoder_1_out5, decoder_1_out6,
       decoder_1_out7;
  wire [31:0] Register1_q, Register2_q, Register3_q, Register4_q, Register5_q, Register6_q, Register7_q;

  Decoder #(.select(3), .enable("false")) decoder_1 (
    .out0(decoder_1_out0), .out1(decoder_1_out1), .out2(decoder_1_out2), .out3(decoder_1_out3),
    .out4(decoder_1_out4), .out5(decoder_1_out5), .out6(decoder_1_out6), .out7(decoder_1_out7),
    .sel(WriteRegister[2:0]));
  and and_1 (and_1_out, decoder_1_out1, RegisterWrite);
  and and_2 (and_2_out, decoder_1_out2, RegisterWrite);
  and and_3 (and_3_out, decoder_1_out3, RegisterWrite);
  and and_4 (and_4_out, decoder_1_out4, RegisterWrite);
  and and_5 (and_5_out, decoder_1_out5, RegisterWrite);
  and and_6 (and_6_out, decoder_1_out6, RegisterWrite);
  and and_7 (and_7_out, decoder_1_out7, RegisterWrite);
  Register #(.width(32)) Register1 (.D(WriteData), .en(and_1_out), .Q(Register1_q), .clk(Clock));  // open: clr
  Register #(.width(32)) Register2 (.D(WriteData), .en(and_2_out), .Q(Register2_q), .clk(Clock));  // open: clr
  Register #(.width(32)) Register3 (.D(WriteData), .en(and_3_out), .Q(Register3_q), .clk(Clock));  // open: clr
  Register #(.width(32)) Register4 (.D(WriteData), .en(and_4_out), .Q(Register4_q), .clk(Clock));  // open: clr
  Register #(.width(32)) Register5 (.D(WriteData), .en(and_5_out), .Q(Register5_q), .clk(Clock));  // open: clr
  Register #(.width(32)) Register6 (.D(WriteData), .en(and_6_out), .Q(Register6_q), .clk(Clock));  // open: clr
  Register #(.width(32)) Register7 (.D(WriteData), .en(and_7_out), .Q(Register7_q), .clk(Clock));  // open: clr
  Multiplexer #(.select(3), .width(32), .enable("false")) multiplexer_1 (
    .in0({32{1'b0}}), .in1(Register1_q), .in2(Register2_q), .in3(Register3_q), .in4(Register4_q),
    .in5(Register5_q), .in6(Register6_q), .in7(Register7_q), .out(Read0_2), .sel(Read0[2:0]));
  Multiplexer #(.select(3), .width(32), .enable("false")) multiplexer_2 (
    .in0({32{1'b0}}), .in1(Register1_q), .in2(Register2_q), .in3(Register3_q), .in4(Register4_q),
    .in5(Register5_q), .in6(Register6_q), .in7(Register7_q), .out(Read1_2), .sel(Read1[2:0]));
  // also tied to GND on the sheet: decoder_1_out0
endmodule
