// Logisim project 4BitAdderSubtracer.circ as structural Verilog: 2 circuits, main circuit main
module main (
  input  [3:0] A,
  input  [3:0] B,
  input  Sub,
  output [3:0] out_4,
  output Cout4
);

  wire fas_1_cout, fas_2_cout, fas_3_cout;

  fas fas_1 (.A(A[0]), .B(B[0]), .Cin(Sub), .Sub(Sub), .S(out_4[0]), .Cout(fas_1_cout));
  fas fas_2 (.A(A[1]), .B(B[1]), .Cin(fas_1_cout), .Sub(Sub), .S(out_4[1]), .Cout(fas_2_cout));
  fas fas_3 (.A(A[2]), .B(B[2]), .Cin(fas_2_cout), .Sub(Sub), .S(out_4[2]), .Cout(fas_3_cout));
  fas fas_4 (.A(A[3]), .B(B[3]), .Cin(fas_3_cout), .Sub(Sub), .S(out_4[3]), .Cout(Cout4));
endmodule

module fas (
  input  A,
  input  B,
  input  Cin,
  input  Sub,
  output S,
  output Cout
);

  wire and_1_out, and_2_out, multiplexer_1_out, not_1_out, xor_1_out;

  Multiplexer multiplexer_1 (.in0(B), .in1(not_1_out), .out(multiplexer_1_out), .sel(Sub));  // open: en
  not not_1 (not_1_out, B);
  xor xor_1 (xor_1_out, A, multiplexer_1_out);
  xor xor_2 (S, xor_1_out, Cin);
  and and_1 (and_1_out, xor_1_out, Cin);
  and and_2 (and_2_out, A, multiplexer_1_out);
  or or_1 (Cout, and_1_out, and_2_out);
endmodule
