// Logisim project True if greater than 11.circ as structural Verilog: 1 circuit, main circuit main
module main (
  input  in_1,
  input  in_2,
  input  in_3,
  input  in_4
);

  wire and_1_out, and_2_out, nor_1_out, or_1_out, or_2_out;

  and and_1 (and_1_out, in_1, in_2);
  // Probe on and_2_out
  and and_2 (and_2_out, and_1_out, or_1_out);
  or or_1 (or_1_out, or_2_out, nor_1_out);
  or or_2 (or_2_out, in_3, in_4);
  nor nor_1 (nor_1_out, in_3, in_4);
endmodule
